# Fritzing sketch schematic-bipolar (saved by Fritzing 0.9.3b)
breadboards: 1

parts:
  Part1 = Arduino Nano (Rev3.0)
  C1 = Electrolytic Capacitor [capacitance=10µF package="100 mil [THT, electrolytic]"]
  R1 = Resistor [tolerance=±1% resistance=10k package=THT]
  M1 = Stepper Motor - Bipolar
  Power_plug1 = Power plug
  Pololu_A1 = Pololu A4988 [package=SO16]
  C2 = Electrolytic Capacitor [capacitance=100µF voltage=50V package="100 mil [THT, electrolytic]"]
  R2 = Temperature Sensor (Thermistor) [thermistor_type=NTC package=THT]

nets:
  N1: Part1.RESET, C1.+
  N2: Part1.GND, C1.-, Pololu_A1.GND#8, R2.pin_1
  N3: Part1.D7, Pololu_A1.DIR
  N4: Part1.D8, Pololu_A1.STEP
  N5: Part1.D9, Pololu_A1.SLEEP
  N6: Part1.D10, Pololu_A1.MS3
  N7: Part1.D11/MOSI, Pololu_A1.MS2
  N8: Part1.D12/MISO, Pololu_A1.MS1
  5V: Part1.5V, Pololu_A1.RESET, Pololu_A1.VDD
  N9: Part1.A0, R1.Pin_1, R2.pin_0
  N10: Part1.AREF, R1.Pin_0
  N11: M1.A, Pololu_A1.2B
  N12: M1.C, Pololu_A1.2A
  N13: M1.B, Pololu_A1.1A
  N14: M1.D, Pololu_A1.1B
  N15: Power_plug1.GND, Pololu_A1.GND#14, C2.-
  N16: Power_plug1.VCC, Pololu_A1.VMOT, C2.+

notes:
  +12V
