# Fritzing sketch schematic-unipolar (saved by Fritzing 0.9.3b)

parts:
  Part1 = Arduino Nano (Rev3.0)
  C1 = Electrolytic Capacitor [capacitance=10µF package="100 mil [THT, electrolytic]"]
  R1 = Resistor [tolerance=±1% resistance=10k package=THT]
  Power_plug1 = Power plug
  BREAKOUT1 = prefix101227
  R2 = Temperature Sensor (Thermistor) [thermistor_type=NTC part_number=10K package=THT]
  MOTOR1 = 28BYJ-48 Stepper Motor  # not connected

nets:
  N1: Part1.RESET, C1.+
  N2: Part1.GND, C1.-, R2.pin_1
  N3: Part1.D8, BREAKOUT1.connector0
  N4: Part1.D9, BREAKOUT1.connector1
  N5: Part1.D10, BREAKOUT1.connector2
  N6: Part1.D11/MOSI, BREAKOUT1.connector3
  N7: Part1.A0, R1.Pin_1, R2.pin_0
  N8: Part1.AREF, Part1.3V3, R1.Pin_0
  N9: Power_plug1.GND, BREAKOUT1.connector7
  N10: Power_plug1.VCC, BREAKOUT1.connector8

notes:
  +12V
